# Fritzing sketch meteo (saved by Fritzing 0.9.5d)
perfboards: 1

parts:
  OLED1 = OLED 128x64 I2C Monochrome Display
  Componente3 = BME280 Breakout
  Componente4 = Arduino Nano 33 IOT
  U2 = GAS_SENSOR [package=mq-3]
  R2 = Resistor [tolerance=±5% resistance=51000 package=THT]
  R4 = Resistor [tolerance=±5% resistance=51000 package=THT]

nets:
  GND: OLED1.GND, Componente4.GND, Componente4.D13~, U2.H1
  VDD: OLED1.VDD, Componente3.3.3V, Componente4.3V3, R2.Pin_0, R4.Pin_0
  N1: OLED1.SCK, Componente3.SCK/SCL, Componente4.A6, R2.Pin_1
  N2: OLED1.SDA, Componente3.SDI/SDA, Componente4.A5, R4.Pin_1
  N3: Componente4.RESET, Componente4.A7
  N4: Componente4.D11/MOSI, Componente4.+5V, U2.H2

notes:
  Make sure to solder the 5V jumper on the back of the Nano

custom parts:
  Arduino Nano 33 IOT: The Arduino Nano 33 IoT is the easiest and cheapest point of entry to enhance existing devices (and creating new ones) to be part of the IoT and designing pico-network applications. Whether you are looking at building a sensor network connected to your office or home router, or if you want to create a BLE device sending data to a cellphone, the Nano 33 IoT is your one-stop-solution for many of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
